// Logisim project s-mips.circ as structural Verilog: 22 circuits, main circuit S-MIPS Board
module S_MIPS_Board (
  input  DESHABILITAR_DISPATCHER,
  output halt
);

  wire button_1_out, CLK, CS, d_ff_1_q, LCLR, LoadRAM, LoadRAMOn, LW, R_R_W, R_W, ram_dispatcher_1_finished,
       RCS, Reset_out, RST, TTY_EN;
  wire [2:0] KDB;
  wire [3:0] LMask, Mask, ram_1_read_time, ram_1_write_time, RMask;
  wire [6:0] KDB_DATA, TTY_DATA;
  wire [15:0] Addr, LAddr, RAddr;
  wire [31:0] I0, I1, I2, I3, LData, ram_1_data_out_0, ram_1_data_out_1, ram_1_data_out_2, ram_1_data_out_3,
       RI0, RI1, RI2, RI3;

  TTY #(.rows(25), .cols(80)) tty_1 (.data(TTY_DATA), .clk(CLK), .we(TTY_EN), .clr(RST));
  not not_1 (LoadRAMOn, ram_dispatcher_1_finished);
  RAM_Dispatcher ram_dispatcher_1 (
    .WriteTime(ram_1_write_time), .Clock(CLK), .Data(LData), .Address(LAddr), .Mask(LMask),
    .Finished(ram_dispatcher_1_finished), .Write(LW), .CLR(LCLR));
  Keyboard #(.buflen(64)) keyboard_1 (.clk(CLK), .re(KDB[0]), .avail(KDB[2]), .data(KDB_DATA));  // open: clr
  RAM ram_1 (
    .Address(RAddr), .Data_Out_0(ram_1_data_out_0), .Data_Out_1(ram_1_data_out_1),
    .Data_Out_2(ram_1_data_out_2), .Data_Out_3(ram_1_data_out_3), .Data_In_0(RI0), .Data_In_1(RI1),
    .Data_In_2(RI2), .Data_In_3(RI3), .Mask(RMask), .nRead_Write(R_R_W), .Chip_Select(RCS),
    .Read_Time(ram_1_read_time), .Reset(button_1_out), .Write_Time(ram_1_write_time));
  Button button_1 (.out(button_1_out));
  D_Flip_Flop d_ff_1 (.clk(CLK), .D(1'b1), .Q(d_ff_1_q), .reset(Reset_out));  // open: Qn, preset, en
  Button Reset (.out(Reset_out));
  S_MIPS s_mips_1 (
    .Kbd_Enable(KDB[0]), .Address(Addr), .Kbd_Clear(KDB[1]), .Kbd_Available(KDB[2]), .RAM_In_0(I0),
    .Kbd_ASCII_Data(KDB_DATA), .RAM_In_1(I1), .TTY_Enable(TTY_EN), .RAM_In_2(I2), .RAM_In_3(I3),
    .TTY_ASCII_Data(TTY_DATA), .Reset(RST), .RAM_Out_0(ram_1_data_out_0), .Clock(CLK),
    .RAM_Out_1(ram_1_data_out_1), .Stop(halt), .RAM_Out_2(ram_1_data_out_2), .RAM_Out_3(ram_1_data_out_3),
    .Mask(Mask), .Read_Time(ram_1_read_time), .Write_Time(ram_1_write_time), .nRead_Write(R_W),
    .Chip_Select(CS));
  D_Flip_Flop d_ff_2 (.clk(CLK), .D(d_ff_1_q), .Qn(LCLR), .reset(Reset_out));  // open: Q, preset, en
  or or_1 (RST, LCLR, LoadRAM);
  Clock clock_1 (.out(CLK));
  Multiplexer #(.width(32), .enable("false")) multiplexer_1 (.in0(I0), .in1(LData), .out(RI0), .sel(LoadRAM));
  Multiplexer #(.width(32), .enable("false")) multiplexer_2 (.in0(I1), .in1(LData), .out(RI1), .sel(LoadRAM));
  Multiplexer #(.width(32), .enable("false")) multiplexer_3 (.in0(I2), .in1(LData), .out(RI2), .sel(LoadRAM));
  Multiplexer #(.width(32), .enable("false")) multiplexer_4 (.in0(I3), .in1(LData), .out(RI3), .sel(LoadRAM));
  // OR_Gate or_2 is placed but not wired
  and and_1 (LoadRAM, ~DESHABILITAR_DISPATCHER, LoadRAMOn);  // AND_Gate
  Multiplexer #(.width(16), .enable("false")) multiplexer_5 (.in0(Addr), .in1(LAddr), .out(RAddr), .sel(LoadRAM));
  Multiplexer #(.width(4), .enable("false")) multiplexer_6 (.in0(Mask), .in1(LMask), .out(RMask), .sel(LoadRAM));
  Multiplexer #(.enable("false")) multiplexer_7 (.in0(CS), .in1(LW), .out(RCS), .sel(LoadRAM));
  Multiplexer #(.enable("false")) multiplexer_8 (.in0(R_W), .in1(LW), .out(R_R_W), .sel(LoadRAM));

  // Notes on the sheet:
  //   NO MODIFICAR
  //   Keyboard
endmodule

module RAM (
  input  [15:0] Address,
  input  [31:0] Data_In_0,
  input  [31:0] Data_In_1,
  input  [31:0] Data_In_2,
  input  [31:0] Data_In_3,
  input  [3:0] Mask,
  input  nRead_Write,
  input  Chip_Select,
  input  Reset,
  output [31:0] Data_Out_0,
  output [31:0] Data_Out_1,
  output [31:0] Data_Out_2,
  output [31:0] Data_Out_3,
  output [3:0] Read_Time,
  output [3:0] Write_Time
);

  wire and_2_out, and_3_out, and_4_out, and_5_out, and_6_out, and_7_out, and_8_out, and_9_out, Changed, CLK,
       comparator_2_eq, comparator_3_eq, comparator_4_eq, comparator_5_eq, comparator_6_eq, Count,
       demultiplexer_3_out0, Idle, Idle_q, Load, Load0, Load1, nand_1_out, or_1_out, or_2_out, or_3_out,
       or_4_out, or_5_out, or_6_out, or_7_out, or_8_out, or_9_out, or_10_out, Proc_q, Update_Mem, Zero_Time;
  wire [3:0] counter_1_q, multiplexer_1_out, subtractor_1_out;
  wire [31:0] register_1_q, register_2_q, register_3_q, register_4_q, register_5_q;

  // Probe on 4'b0011
  // Probe on 4'b0010
  Multiplexer #(.width(4), .enable("false")) multiplexer_1 (
    .in0(4'b0011), .in1(4'b0010), .out(multiplexer_1_out), .sel(nRead_Write));
  or or_1 (or_1_out, Idle, Update_Mem);
  or or_2 (or_2_out, ~Chip_Select, Reset);  // OR_Gate
  Subtractor #(.width(4)) subtractor_1 (.a(multiplexer_1_out), .b(4'b0010), .out(subtractor_1_out));  // open: bin, bout
  D_Flip_Flop u_Idle (.clk(CLK), .D(or_1_out), .Q(Idle_q), .preset(or_2_out));  // open: Qn, en, reset
  Demultiplexer #(.enable("false")) demultiplexer_1 (.out0(Idle), .out1(Load0), .in(Idle_q), .sel(Changed));
  // Probe on counter_1_q
  Counter #(.width(4), .max('hf)) counter_1 (
    .load(Load), .D(subtractor_1_out), .count(Count), .Q(counter_1_q), .clk(CLK), .clr(or_3_out));  // open: carry
  or or_3 (or_3_out, ~Chip_Select, Reset);  // OR_Gate
  Comparator #(.width(4), .mode("unsigned")) comparator_1 (
    .a(4'b0000), .b(counter_1_q), .eq(Zero_Time));  // open: gt, lt
  or or_4 (or_4_out, Count, Load0, Load1);
  Register #(.width(32)) register_1 (.D(Data_In_0), .en(Chip_Select), .Q(register_1_q), .clk(CLK), .clr(or_5_out));
  or or_5 (or_5_out, ~Chip_Select, Reset);  // OR_Gate
  Register #(.width(32)) register_2 (.D(Data_In_1), .en(Chip_Select), .Q(register_2_q), .clk(CLK), .clr(or_6_out));
  or or_6 (or_6_out, ~Chip_Select, Reset);  // OR_Gate
  Register #(.width(32)) register_3 (.D(Data_In_2), .en(Chip_Select), .Q(register_3_q), .clk(CLK), .clr(or_7_out));
  or or_7 (or_7_out, ~Chip_Select, Reset);  // OR_Gate
  Register #(.width(32)) register_4 (.D(Data_In_3), .en(Chip_Select), .Q(register_4_q), .clk(CLK), .clr(or_8_out));
  or or_8 (or_8_out, ~Chip_Select, Reset);  // OR_Gate
  Register #(.width(32)) register_5 (
    .D({{11{1'b1}}, nRead_Write, Mask, Address}), .en(Chip_Select), .Q(register_5_q), .clk(CLK),
    .clr(or_9_out));
  or or_9 (or_9_out, ~Chip_Select, Reset);  // OR_Gate
  D_Flip_Flop Proc (.clk(CLK), .D(or_4_out), .Q(Proc_q), .reset(or_10_out));  // open: Qn, preset, en
  or or_10 (or_10_out, ~Chip_Select, Reset);  // OR_Gate
  Demultiplexer #(.enable("false")) demultiplexer_2 (
    .out0(Count), .out1(Update_Mem), .in(demultiplexer_3_out0), .sel(Zero_Time));
  Demultiplexer #(.enable("false")) demultiplexer_3 (
    .out0(demultiplexer_3_out0), .out1(Load1), .in(Proc_q), .sel(Changed));
  Clock clock_1 (.out(CLK));
  Comparator #(.width(32)) comparator_2 (.a(register_1_q), .b(Data_In_0), .eq(comparator_2_eq));  // open: gt, lt
  Comparator #(.width(32)) comparator_3 (.a(register_2_q), .b(Data_In_1), .eq(comparator_3_eq));  // open: gt, lt
  Comparator #(.width(32)) comparator_4 (.a(register_3_q), .b(Data_In_2), .eq(comparator_4_eq));  // open: gt, lt
  Comparator #(.width(32)) comparator_5 (.a(register_4_q), .b(Data_In_3), .eq(comparator_5_eq));  // open: gt, lt
  Comparator #(.width(32)) comparator_6 (
    .a(register_5_q), .b({{11{1'b1}}, nRead_Write, Mask, Address}), .eq(comparator_6_eq));  // open: gt, lt
  nand nand_1 (nand_1_out, comparator_6_eq, comparator_2_eq, comparator_3_eq, comparator_4_eq, comparator_5_eq);
  and and_1 (Changed, nand_1_out, Chip_Select);
  or or_11 (Load, Count, Load1, Load0);
  and and_2 (and_2_out, Mask[0], Update_Mem, nRead_Write);
  and and_3 (and_3_out, Mask[1], Update_Mem, nRead_Write);
  and and_4 (and_4_out, Mask[2], Update_Mem, nRead_Write);
  and and_5 (and_5_out, Mask[3], Update_Mem, nRead_Write);
  // Probe on Data_Out_0
  RAM_part #(.addrWidth(16), .dataWidth(32), .bus("separate")) ram_1 (
    .addr(Address), .din(Data_In_0), .data(Data_Out_0), .str(and_2_out), .sel(Chip_Select), .clk(CLK),
    .ld(and_6_out), .clr(Reset));
  and and_6 (and_6_out, ~nRead_Write, Idle);  // AND_Gate
  RAM_part #(.addrWidth(16), .dataWidth(32), .bus("separate")) ram_2 (
    .addr(Address), .din(Data_In_1), .data(Data_Out_1), .str(and_3_out), .sel(Chip_Select), .clk(CLK),
    .ld(and_7_out), .clr(Reset));
  and and_7 (and_7_out, ~nRead_Write, Idle);  // AND_Gate
  RAM_part #(.addrWidth(16), .dataWidth(32), .bus("separate")) ram_3 (
    .addr(Address), .din(Data_In_2), .data(Data_Out_2), .str(and_4_out), .sel(Chip_Select), .clk(CLK),
    .ld(and_8_out), .clr(Reset));
  and and_8 (and_8_out, ~nRead_Write, Idle);  // AND_Gate
  RAM_part #(.addrWidth(16), .dataWidth(32), .bus("separate")) ram_4 (
    .addr(Address), .din(Data_In_3), .data(Data_Out_3), .str(and_5_out), .sel(Chip_Select), .clk(CLK),
    .ld(and_9_out), .clr(Reset));
  and and_9 (and_9_out, ~nRead_Write, Idle);  // AND_Gate

  assign Read_Time = 4'b0011;
  assign Write_Time = 4'b0010;

  // Other names for the same wires on the sheet: M0 = Mask[0]; M1 = Mask[1]; M2 = Mask[2]; M3 = Mask[3];
  //   RW = nRead_Write; CLR = Reset; CS = Chip_Select; Load2 = Count

  // Notes on the sheet:
  //   NO MODIFICAR
  //   excepto quizás los valores RT y WT
  //   BANK0
  //   BANK1
  //   BANK2
  //   BANK3
endmodule

module S_MIPS (
  input  Kbd_Available,
  input  [6:0] Kbd_ASCII_Data,
  input  [31:0] RAM_Out_0,
  input  [31:0] RAM_Out_1,
  input  Reset,
  input  [31:0] RAM_Out_2,
  input  Clock,
  input  [31:0] RAM_Out_3,
  input  [3:0] Read_Time,
  input  [3:0] Write_Time,
  output Kbd_Enable,
  output [15:0] Address,
  output Kbd_Clear,
  output TTY_Enable,
  output [6:0] TTY_ASCII_Data,
  output Stop,
  output [31:0] RAM_In_0,
  output [31:0] RAM_In_1,
  output [31:0] RAM_In_2,
  output [31:0] RAM_In_3,
  output [3:0] Mask,
  output nRead_Write,
  output Chip_Select
);

  wire AluI, d_ff_2_q, EnablerGI, EnablerPC, EnablerRF, GetData, GetI, Halt, JumpI, MemoryI, MemoryI_star,
       or_1_out, ReadyData, ReadyI, ReadyW, RI, StackI, Start, Tty, Write, WriteI;
  wire [31:0] Address_t, Bank0, Bank1, Bank2, Bank3, BankOut0, BankOut1, BankOut2, BankOut3, DataIn,
       datapath_1_rout;

  D_Flip_Flop #(.trigger("falling")) d_ff_1 (.clk(Clock), .D(Reset), .Q(Start));  // open: Qn, preset, en, reset
  Multiplexer #(.width(32), .enable("false")) multiplexer_1 (.in0(RAM_Out_0), .in1(RAM_In_0), .out(Bank0), .sel(Write));
  Multiplexer #(.width(32), .enable("false")) multiplexer_2 (.in0(RAM_Out_1), .in1(RAM_In_0), .out(Bank1), .sel(Write));
  Multiplexer #(.width(32), .enable("false")) multiplexer_3 (.in0(RAM_Out_2), .in1(RAM_In_0), .out(Bank2), .sel(Write));
  Multiplexer #(.width(32), .enable("false")) multiplexer_4 (.in0(RAM_Out_3), .in1(RAM_In_0), .out(Bank3), .sel(Write));
  D_Flip_Flop #(.trigger("falling")) d_ff_2 (
    .clk(Clock), .D(GetI), .Q(d_ff_2_q), .en(or_1_out));  // open: Qn, preset, reset
  or or_1 (or_1_out, GetI, ReadyI);
  Control_Unit control_unit_1 (
    .Clk(Clock), .Start(Start), .AluI(AluI), .JumpI(JumpI), .MemoryI(MemoryI_star), .RI(RI), .Reset(Reset),
    .ReadyData(ReadyData), .WriteI(WriteI), .ReadyI(ReadyI), .ReadyW(ReadyW), .TtyI(Tty), .End(Stop),
    .TtyEn(TTY_Enable), .Write(Write), .GetData(GetData), .UseGI(EnablerGI), .UseRF(EnablerRF),
    .KeyboardEN(Kbd_Enable), .GetI(GetI), .UsePC(EnablerPC));
  DataPath datapath_1 (
    .clk(Clock), .KeyboardInput(Kbd_ASCII_Data), .Instruction(DataIn), .Reset(Reset), .EnablerRF(EnablerRF),
    .EnablerPC(EnablerPC), .EnablerGI(EnablerGI), .NextOk(d_ff_2_q), .WriteI(WriteI), .ALUI(AluI),
    .StackI(StackI), .MemoryI(MemoryI), .Tty(Tty), .JumpI(JumpI), .RI(RI), .Halt(Halt),
    .TtyData(TTY_ASCII_Data), .Address(Address_t), .ROut(datapath_1_rout), .KeyboardAva(Kbd_Available));
  I_O i_o_1 (.in_1(datapath_1_rout), .Output(RAM_In_0));
  Ram_Interact ram_interact_1 (
    .Bank0(Bank0), .Bank1(Bank1), .Bank2(Bank2), .Bank3(Bank3), .DPAddress(Address_t), .ReadTime(Read_Time),
    .WriteTime(Write_Time), .Clk(Clock), .Reset(Reset), .Write(Write), .GetI(GetI), .GetData(GetData),
    .IsI(EnablerGI), .BankOut0(BankOut0), .BankOut1(BankOut1), .BankOut2(BankOut2), .BankOut3(BankOut3),
    .MASK(Mask), .RW(nRead_Write), .CS(Chip_Select), .ReadyI(ReadyI), .ReadyData(ReadyData),
    .ReadyWrite(ReadyW), .ADDR(Address));
  or or_2 (MemoryI_star, MemoryI, StackI);
  Multiplexer #(.select(2), .width(32), .enable("false")) multiplexer_5 (
    .in0(BankOut0), .in1(BankOut1), .in2(BankOut2), .in3(BankOut3), .out(DataIn), .sel(Address_t[3:2]));
  // Probe on DataIn

  assign Kbd_Clear = Reset;
  assign RAM_In_1 = RAM_In_0;
  assign RAM_In_2 = RAM_In_0;
  assign RAM_In_3 = RAM_In_0;

  // Other names for the same wires on the sheet: CLK = Clock; CS = Chip_Select; KBD_AVAIL = Kbd_Available;
  //   CLR = Reset; KBD_CLR = Reset; KBD_DATA[6:0] = Kbd_ASCII_Data; RAM_A[15:0] = Address; RAM_MASK[3:0] = Mask;
  //   RAM_OUTPUT_0[31:0] = RAM_Out_0; RAM_OUTPUT_1[31:0] = RAM_Out_1; RAM_OUTPUT_2[31:0] = RAM_Out_2;
  //   RAM_OUTPUT_3[31:0] = RAM_Out_3; RAM_INPUT_0[31:0] = RAM_In_0; RAM_INPUT_1[31:0] = RAM_In_0;
  //   RAM_INPUT_2[31:0] = RAM_In_0; RAM_INPUT_3[31:0] = RAM_In_0; ROut[31:0] = RAM_In_0; RW = nRead_Write;
  //   TTY_DATA[6:0] = TTY_ASCII_Data

  // Notes on the sheet:
  //   RAM ADDRESS
  //   DATA FROM RAM
  //   DATA TO RAM
  //   DATA WRITE MASK
  //   RAM TIMING
  //   RAM CONTROL
  //   KEYBOARD
  //   TTY
  //   SEQUENCING
endmodule

module RAM_Dispatcher (
  input  [3:0] WriteTime,
  input  Clock,
  input  CLR,
  output [31:0] Data,
  output [15:0] Address,
  output [3:0] Mask,
  output Finished,
  output Write
);

  wire demultiplexer_2_out1, demultiplexer_3_out1, End, IDLE_q, IncAddr, Load, or_1_out, or_2_out, While_q,
       WriteEnd;
  wire [3:0] counter_1_q;
  wire [31:0] CurrentAddress_q;

  Counter #(.width(32), .max('hffffffff)) CurrentAddress (
    .count(IncAddr), .Q({CurrentAddress_q[31:18], Address, CurrentAddress_q[1:0]}), .clk(Clock), .clr(CLR));  // open: load, D, carry
  or or_1 (or_1_out, IncAddr, demultiplexer_3_out1, Finished);
  D_Flip_Flop IDLE (.clk(Clock), .D(or_1_out), .Q(IDLE_q), .preset(CLR));  // open: Qn, en, reset
  Demultiplexer #(.enable("false")) demultiplexer_1 (.out0(Load), .out1(Finished), .in(IDLE_q), .sel(End));
  D_Flip_Flop While (.clk(Clock), .D(or_2_out), .Q(While_q), .reset(CLR));  // open: Qn, preset, en
  or or_2 (or_2_out, Write, Load);
  RAM_part #(.addrWidth(18), .dataWidth(32)) ram_1 (
    .addr({Address, CurrentAddress_q[1:0]}), .data(Data), .clk(Clock));  // open: sel, ld, clr
  Demultiplexer #(.enable("false")) demultiplexer_2 (
    .out0(Write), .out1(demultiplexer_2_out1), .in(While_q), .sel(WriteEnd));
  Decoder #(.select(2)) decoder_1 (
    .out0(Mask[0]), .out1(Mask[1]), .out2(Mask[2]), .out3(Mask[3]), .sel(CurrentAddress_q[1:0]));  // open: en
  Demultiplexer #(.enable("false")) demultiplexer_3 (
    .out0(IncAddr), .out1(demultiplexer_3_out1), .in(demultiplexer_2_out1), .sel(End));
  Counter #(.width(4), .max('hf)) counter_1 (
    .load(Load), .D(WriteTime), .count(Write), .Q(counter_1_q), .clk(Clock));  // open: carry, clr
  Comparator #(.width(32)) comparator_1 (.a(Data), .b({32{1'b1}}), .eq(End));  // open: gt, lt
  Comparator #(.width(4)) comparator_2 (.a(4'b0000), .b(counter_1_q), .eq(WriteEnd));  // open: gt, lt

  // Other names for the same wires on the sheet: CLK = Clock; Count = Write; WT[3:0] = WriteTime
endmodule

// ID
module Instruction_Decoder (
  input  [31:0] in_1,
  output Nop,
  output Slt,
  output Jr,
  output Addi,
  output Sw,
  output [25:0] DestinoSalto,
  output Addt,
  output Sltu,
  output Mfhi,
  output Slti,
  output Beq,
  output Sub,
  output And,
  output Mflo,
  output Sltiu,
  output Bne,
  output [15:0] Constante,
  output Mult,
  output Or,
  output Halt,
  output Andi,
  output Blez,
  output Div,
  output Nor,
  output Tty,
  output Ori,
  output Bgtz,
  output [4:0] RS,
  output Mulu,
  output Xor,
  output Rnd,
  output Xori,
  output Bltz,
  output [4:0] RT,
  output Divu,
  output Pop,
  output Kbd,
  output Lw,
  output J,
  output [4:0] RD,
  output Push
);

  wire comparator_2_eq, comparator_3_eq, comparator_4_eq, comparator_5_eq, comparator_6_eq, comparator_7_eq,
       comparator_8_eq, comparator_10_eq, comparator_11_eq, comparator_12_eq, comparator_13_eq,
       comparator_14_eq, comparator_15_eq, comparator_16_eq, comparator_17_eq, comparator_19_eq,
       comparator_20_eq, comparator_21_eq, comparator_22_eq, comparator_23_eq, comparator_24_eq,
       comparator_25_eq, OP0, OP3f, OP38;

  Comparator #(.width(6)) comparator_1 (.a(in_1[31:26]), .b({6{1'b0}}), .eq(OP0));  // open: gt, lt
  Comparator #(.width(6)) comparator_2 (.a(in_1[5:0]), .b({6{1'b0}}), .eq(comparator_2_eq));  // open: gt, lt
  Comparator #(.width(6)) comparator_3 (.a(in_1[5:0]), .b(6'b100000), .eq(comparator_3_eq));  // open: gt, lt
  Comparator #(.width(6)) comparator_4 (.a(in_1[5:0]), .b(6'b100010), .eq(comparator_4_eq));  // open: gt, lt
  Comparator #(.width(6)) comparator_5 (.a(in_1[5:0]), .b(6'b011000), .eq(comparator_5_eq));  // open: gt, lt
  Comparator #(.width(6)) comparator_6 (.a(in_1[5:0]), .b(6'b011010), .eq(comparator_6_eq));  // open: gt, lt
  Comparator #(.width(6)) comparator_7 (.a(in_1[5:0]), .b(6'b011001), .eq(comparator_7_eq));  // open: gt, lt
  Comparator #(.width(6)) comparator_8 (.a(in_1[5:0]), .b(6'b011011), .eq(comparator_8_eq));  // open: gt, lt
  and and_1 (Nop, OP0, comparator_2_eq);
  and and_2 (Addt, OP0, comparator_3_eq);
  and and_3 (Sub, OP0, comparator_4_eq);
  and and_4 (Mult, OP0, comparator_5_eq);
  and and_5 (Div, OP0, comparator_6_eq);
  and and_6 (Mulu, OP0, comparator_7_eq);
  and and_7 (Divu, OP0, comparator_8_eq);
  Comparator #(.width(6)) comparator_9 (.a(in_1[31:26]), .b({6{1'b1}}), .eq(OP3f));  // open: gt, lt
  Comparator #(.width(6)) comparator_10 (.a(in_1[5:0]), .b(6'b101010), .eq(comparator_10_eq));  // open: gt, lt
  Comparator #(.width(6)) comparator_11 (.a(in_1[5:0]), .b(6'b101011), .eq(comparator_11_eq));  // open: gt, lt
  Comparator #(.width(6)) comparator_12 (.a(in_1[5:0]), .b(6'b100100), .eq(comparator_12_eq));  // open: gt, lt
  Comparator #(.width(6)) comparator_13 (.a(in_1[5:0]), .b(6'b100101), .eq(comparator_13_eq));  // open: gt, lt
  Comparator #(.width(6)) comparator_14 (.a(in_1[5:0]), .b(6'b100111), .eq(comparator_14_eq));  // open: gt, lt
  Comparator #(.width(6)) comparator_15 (.a(in_1[5:0]), .b(6'b101000), .eq(comparator_15_eq));  // open: gt, lt
  Comparator #(.width(6)) comparator_16 (.a(in_1[5:0]), .b({6{1'b0}}), .eq(comparator_16_eq));  // open: gt, lt
  Comparator #(.width(6)) comparator_17 (.a(in_1[5:0]), .b(6'b000001), .eq(comparator_17_eq));  // open: gt, lt
  and and_8 (Slt, OP0, comparator_10_eq);
  and and_9 (Sltu, OP0, comparator_11_eq);
  and and_10 (And, OP0, comparator_12_eq);
  and and_11 (Or, OP0, comparator_13_eq);
  and and_12 (Nor, OP0, comparator_14_eq);
  and and_13 (Xor, OP0, comparator_15_eq);
  and and_14 (Pop, OP38, comparator_16_eq);
  and and_15 (Push, OP38, comparator_17_eq);
  Comparator #(.width(6)) comparator_18 (.a(in_1[31:26]), .b(6'b111000), .eq(OP38));  // open: gt, lt
  Comparator #(.width(6)) comparator_19 (.a(in_1[5:0]), .b(6'b001000), .eq(comparator_19_eq));  // open: gt, lt
  Comparator #(.width(6)) comparator_20 (.a(in_1[5:0]), .b(6'b010000), .eq(comparator_20_eq));  // open: gt, lt
  Comparator #(.width(6)) comparator_21 (.a(in_1[5:0]), .b(6'b010010), .eq(comparator_21_eq));  // open: gt, lt
  Comparator #(.width(6)) comparator_22 (.a(in_1[5:0]), .b({6{1'b1}}), .eq(comparator_22_eq));  // open: gt, lt
  Comparator #(.width(6)) comparator_23 (.a(in_1[5:0]), .b(6'b000001), .eq(comparator_23_eq));  // open: gt, lt
  Comparator #(.width(6)) comparator_24 (.a(in_1[5:0]), .b(6'b000010), .eq(comparator_24_eq));  // open: gt, lt
  Comparator #(.width(6)) comparator_25 (.a(in_1[5:0]), .b(6'b000100), .eq(comparator_25_eq));  // open: gt, lt
  and and_16 (Jr, OP0, comparator_19_eq);
  and and_17 (Mfhi, OP0, comparator_20_eq);
  and and_18 (Mflo, OP0, comparator_21_eq);
  and and_19 (Halt, OP3f, comparator_22_eq);
  and and_20 (Tty, OP3f, comparator_23_eq);
  and and_21 (Rnd, OP3f, comparator_24_eq);
  and and_22 (Kbd, OP3f, comparator_25_eq);
  Comparator #(.width(6)) comparator_26 (.a(in_1[31:26]), .b(6'b001000), .eq(Addi));  // open: gt, lt
  Comparator #(.width(6)) comparator_27 (.a(in_1[31:26]), .b(6'b001010), .eq(Slti));  // open: gt, lt
  Comparator #(.width(6)) comparator_28 (.a(in_1[31:26]), .b(6'b001011), .eq(Sltiu));  // open: gt, lt
  Comparator #(.width(6)) comparator_29 (.a(in_1[31:26]), .b(6'b001100), .eq(Andi));  // open: gt, lt
  Comparator #(.width(6)) comparator_30 (.a(in_1[31:26]), .b(6'b001101), .eq(Ori));  // open: gt, lt
  Comparator #(.width(6)) comparator_31 (.a(in_1[31:26]), .b(6'b001110), .eq(Xori));  // open: gt, lt
  Comparator #(.width(6)) comparator_32 (.a(in_1[31:26]), .b(6'b100011), .eq(Lw));  // open: gt, lt
  Comparator #(.width(6)) comparator_33 (.a(in_1[31:26]), .b(6'b101011), .eq(Sw));  // open: gt, lt
  Comparator #(.width(6)) comparator_34 (.a(in_1[31:26]), .b(6'b000100), .eq(Beq));  // open: gt, lt
  Comparator #(.width(6)) comparator_35 (.a(in_1[31:26]), .b(6'b000101), .eq(Bne));  // open: gt, lt
  Comparator #(.width(6)) comparator_36 (.a(in_1[31:26]), .b(6'b000110), .eq(Blez));  // open: gt, lt
  Comparator #(.width(6)) comparator_37 (.a(in_1[31:26]), .b(6'b000111), .eq(Bgtz));  // open: gt, lt
  Comparator #(.width(6)) comparator_38 (.a(in_1[31:26]), .b(6'b000001), .eq(Bltz));  // open: gt, lt
  Comparator #(.width(6)) comparator_39 (.a(in_1[31:26]), .b(6'b000010), .eq(J));  // open: gt, lt

  assign Constante = in_1[15:0];
  assign DestinoSalto = in_1[25:0];
  assign RD = in_1[15:11];
  assign RS = in_1[25:21];
  assign RT = in_1[20:16];

  // Other names for the same wires on the sheet: add = Addt; FuncCode[5:0] = in_1[5:0]; X[4:0] = in_1[10:6];
  //   OpCode[5:0] = in_1[31:26]

  // Notes on the sheet:
  //   Entrada
endmodule

// RF
module Register_File (
  input  clk,
  input  [31:0] Input,
  input  reset,
  input  write,
  input  pop,
  input  [4:0] Dest,
  input  push,
  input  [4:0] A,
  input  PCEn,
  input  [4:0] B,
  output [31:0] StackPointer,
  output [31:0] Output_A,
  output [31:0] Output_B
);

  wire and_1_out, enable31, or_1_out, R0, R1, R2, R3, R4, R5, R6, R7, R8, R9, R10, R11, R12, R13, R14, R15,
       R16, R17, R18, R19, R20, R21, R22, R23, R24, R25, R26, R27, R28, R29, R30, R31;
  wire [31:0] adder_1_out, multiplexer_3_out, multiplexer_4_out, multiplexer_5_out, O0, O1, O2, O3, O4, O5,
       O6, O7, O8, O9, O10, O11, O12, O13, O14, O15, O16, O17, O18, O19, O20, O21, O22, O23, O24, O25, O26,
       O27, O28, O29, O30, subtractor_1_out;

  // Probe on O1
  Demultiplexer #(.select(5), .enable("false")) demultiplexer_1 (
    .out0(R0), .out1(R1), .out2(R2), .out3(R3), .out4(R4), .out5(R5), .out6(R6), .out7(R7), .out8(R8),
    .out9(R9), .out10(R10), .out11(R11), .out12(R12), .out13(R13), .out14(R14), .out15(R15), .out16(R16),
    .out17(R17), .out18(R18), .out19(R19), .out20(R20), .out21(R21), .out22(R22), .out23(R23), .out24(R24),
    .out25(R25), .out26(R26), .out27(R27), .out28(R28), .out29(R29), .out30(R30), .out31(R31), .in(write),
    .sel(Dest));
  // Probe on O2
  Register #(.width(32)) register_1 (.D(Input), .en(R1), .Q(O1), .clk(clk), .clr(reset));
  Register #(.width(32)) register_2 (.D(Input), .en(R9), .Q(O9), .clk(clk), .clr(reset));
  Register #(.width(32)) register_3 (.D(Input), .en(R17), .Q(O17), .clk(clk), .clr(reset));
  Register #(.width(32)) register_4 (.D(Input), .en(R25), .Q(O25), .clk(clk), .clr(reset));
  Multiplexer #(.select(5), .width(32), .enable("false")) multiplexer_1 (
    .in0(O0), .in1(O1), .in2(O2), .in3(O3), .in4(O4), .in5(O5), .in6(O6), .in7(O7), .in8(O8), .in9(O9),
    .in10(O10), .in11(O11), .in12(O12), .in13(O13), .in14(O14), .in15(O15), .in16(O16), .in17(O17),
    .in18(O18), .in19(O19), .in20(O20), .in21(O21), .in22(O22), .in23(O23), .in24(O24), .in25(O25),
    .in26(O26), .in27(O27), .in28(O28), .in29(O29), .in30(O30), .in31(StackPointer), .out(Output_A), .sel(A));
  // Probe on O3
  Register #(.width(32)) register_5 (.D(Input), .en(R2), .Q(O2), .clk(clk), .clr(reset));
  Register #(.width(32)) register_6 (.D(Input), .en(R10), .Q(O10), .clk(clk), .clr(reset));
  Register #(.width(32)) register_7 (.D(Input), .en(R18), .Q(O18), .clk(clk), .clr(reset));
  Register #(.width(32)) register_8 (.D(Input), .en(R26), .Q(O26), .clk(clk), .clr(reset));
  Register #(.width(32)) register_9 (.D(Input), .en(R3), .Q(O3), .clk(clk), .clr(reset));
  Register #(.width(32)) register_10 (.D(Input), .en(R11), .Q(O11), .clk(clk), .clr(reset));
  Register #(.width(32)) register_11 (.D(Input), .en(R19), .Q(O19), .clk(clk), .clr(reset));
  Register #(.width(32)) register_12 (.D(Input), .en(R27), .Q(O27), .clk(clk), .clr(reset));
  Multiplexer #(.select(5), .width(32), .enable("false")) multiplexer_2 (
    .in0(O0), .in1(O1), .in2(O2), .in3(O3), .in4(O4), .in5(O5), .in6(O6), .in7(O7), .in8(O8), .in9(O9),
    .in10(O10), .in11(O11), .in12(O12), .in13(O13), .in14(O14), .in15(O15), .in16(O16), .in17(O17),
    .in18(O18), .in19(O19), .in20(O20), .in21(O21), .in22(O22), .in23(O23), .in24(O24), .in25(O25),
    .in26(O26), .in27(O27), .in28(O28), .in29(O29), .in30(O30), .in31(StackPointer), .out(Output_B), .sel(B));
  Register #(.width(32)) register_13 (.D(Input), .en(R4), .Q(O4), .clk(clk), .clr(reset));
  Register #(.width(32)) register_14 (.D(Input), .en(R12), .Q(O12), .clk(clk), .clr(reset));
  Register #(.width(32)) register_15 (.D(Input), .en(R20), .Q(O20), .clk(clk), .clr(reset));
  Register #(.width(32)) register_16 (.D(Input), .en(R28), .Q(O28), .clk(clk), .clr(reset));
  Register #(.width(32)) register_17 (.D(Input), .en(R5), .Q(O5), .clk(clk), .clr(reset));
  Register #(.width(32)) register_18 (.D(Input), .en(R13), .Q(O13), .clk(clk), .clr(reset));
  Register #(.width(32)) register_19 (.D(Input), .en(R21), .Q(O21), .clk(clk), .clr(reset));
  Register #(.width(32)) register_20 (.D(Input), .en(R29), .Q(O29), .clk(clk), .clr(reset));
  Subtractor #(.width(32)) subtractor_1 (.a(StackPointer), .b(32'h4), .out(subtractor_1_out));  // open: bin, bout
  Adder #(.width(32)) adder_1 (.a(StackPointer), .b(32'h4), .out(adder_1_out));  // open: cin, cout
  Register #(.width(32)) register_21 (.D(Input), .en(R6), .Q(O6), .clk(clk), .clr(reset));
  Register #(.width(32)) register_22 (.D(Input), .en(R14), .Q(O14), .clk(clk), .clr(reset));
  Register #(.width(32)) register_23 (.D(Input), .en(R22), .Q(O22), .clk(clk), .clr(reset));
  Register #(.width(32)) register_24 (.D(Input), .en(R30), .Q(O30), .clk(clk), .clr(reset));
  or or_1 (or_1_out, pop, push);
  Multiplexer #(.width(32), .enable("false")) multiplexer_3 (
    .in0(subtractor_1_out), .in1(adder_1_out), .out(multiplexer_3_out), .sel(pop));
  and and_1 (and_1_out, or_1_out, PCEn);
  Multiplexer #(.width(32), .enable("false")) multiplexer_4 (
    .in0(multiplexer_3_out), .in1({32{1'b1}}), .out(multiplexer_4_out), .sel(reset));
  Register #(.width(32)) register_25 (.D(Input), .en(R7), .Q(O7), .clk(clk), .clr(reset));
  Register #(.width(32)) register_26 (.D(Input), .en(R15), .Q(O15), .clk(clk), .clr(reset));
  Register #(.width(32)) register_27 (.D(Input), .en(R23), .Q(O23), .clk(clk), .clr(reset));
  Register #(.width(32)) register_28 (.en(R0), .Q(O0), .clk(clk), .clr(reset));  // open: D
  or or_2 (enable31, R31, and_1_out, reset);
  Multiplexer #(.width(32), .enable("false")) multiplexer_5 (
    .in0(multiplexer_4_out), .in1(Input), .out(multiplexer_5_out), .sel(R31));
  Register #(.width(32)) register_29 (.D(Input), .en(R8), .Q(O8), .clk(clk), .clr(reset));
  Register #(.width(32)) register_30 (.D(Input), .en(R16), .Q(O16), .clk(clk), .clr(reset));
  Register #(.width(32)) register_31 (.D(Input), .en(R24), .Q(O24), .clk(clk), .clr(reset));
  // Probe on StackPointer
  Register #(.width(32)) register_32 (.D(multiplexer_5_out), .en(enable31), .Q(StackPointer), .clk(clk));  // open: clr

  // Other names for the same wires on the sheet: destination[4:0] = Dest; O31[31:0] = StackPointer; PCenable = PCEn;
  //   selector_A[4:0] = A; selector_B[4:0] = B

  // Notes on the sheet:
  //   Entradas
endmodule

// BC
module Branch_Control (
  input  [31:0] in_1,
  input  [31:0] in_2,
  input  [25:0] in_3,
  input  [15:0] in_4,
  input  in_5,
  input  in_6,
  input  in_7,
  input  [31:0] in_8,
  input  in_9,
  input  in_10,
  input  in_11,
  input  in_12,
  output [31:0] Output
);

  wire and_1_out, and_2_out, and_3_out, and_4_out, and_5_out, comparator_2_eq, Rs_0, Rs__0, Rs_equal_Rt;
  wire [1:0] SelOP;
  wire [31:0] PC_4, PC_4_4Offset;
  wire [31:18] Offset_4;

  Comparator #(.width(32)) comparator_1 (.a(in_8), .b(in_1), .eq(Rs_equal_Rt));  // open: gt, lt
  assign Offset_4 = {{13{in_4[15]}}, in_4[15]};  // Bit_Extender bit_extender_1
  Comparator #(.width(32)) comparator_2 (.a(in_1), .b({32{1'b0}}), .eq(comparator_2_eq), .lt(Rs_0));  // open: gt
  Adder #(.width(32)) adder_1 (.a(in_2), .b(32'h4), .out(PC_4));  // open: cin, cout
  or or_1 (Rs__0, comparator_2_eq, Rs_0);
  Adder #(.width(32)) adder_2 (.a(PC_4), .b({Offset_4, in_4, 2'b00}), .out(PC_4_4Offset));  // open: cin, cout
  Multiplexer #(.select(2), .width(32), .enable("false")) multiplexer_1 (
    .in0(PC_4), .in1(PC_4_4Offset), .in2({in_2[31:28], in_3, 2'b00}), .in3(in_1), .out(Output), .sel(SelOP));
  and and_1 (and_1_out, in_5, Rs_equal_Rt);
  and and_2 (and_2_out, ~Rs_equal_Rt, in_9);  // AND_Gate
  and and_3 (and_3_out, in_12, Rs__0);
  and and_4 (and_4_out, in_10, Rs_0);
  and and_5 (and_5_out, ~Rs__0, in_6);  // AND_Gate
  or or_2 (SelOP[1], in_7, in_11);
  or or_3 (SelOP[0], and_1_out, and_2_out, and_3_out, and_4_out, and_5_out, in_11);

  // Other names for the same wires on the sheet: beq = in_5; bgtz = in_6; blez = in_12; bltz = in_10; bne = in_9;
  //   j = in_7; jr = in_11; Offset[15:0] = in_4; Offset_4[17:2] = in_4; PC[31:0] = in_2; Rs[31:0] = in_1;
  //   Rt[31:0] = in_8; DestinoSalto[25:0] = in_3; Salto[31:2] = {in_2[31:28], in_3}

  // Notes on the sheet:
  //   Entradas
endmodule

// PC
module Program_Counter (
  input  [31:0] in_1,
  input  in_2,
  input  in_3,
  input  in_4,
  output [31:0] Output
);

  Register #(.width(32)) register_1 (.D(in_1), .en(in_2), .Q(Output), .clk(in_4), .clr(in_3));
endmodule

module ALU (
  input  in_1,
  input  [31:0] in_2,
  input  in_3,
  input  [31:0] in_4,
  input  [3:0] in_5,
  input  in_6,
  output [31:0] Output,
  output [31:0] Output_2,
  output [31:0] Output_3
);

  wire Div, Enable, Mult, or_2_out;
  wire [31:0] Add, And, DivHi, DivLo, MultHi, multiplexer_2_out, multiplexer_3_out, MultLo, Nor, Or, Slt,
       Sub, Xor;

  Adder #(.width(32)) adder_1 (.a(in_2), .b(in_4), .out(Add));  // open: cin, cout
  Subtractor #(.width(32)) subtractor_1 (.a(in_2), .b(in_4), .out(Sub));  // open: bin, bout
  assign And = in_2 & in_4;  // AND_Gate and_1, 32 bits wide
  assign Or = in_2 | in_4;  // OR_Gate or_1, 32 bits wide
  assign Nor = ~(in_2 | in_4);  // NOR_Gate nor_1, 32 bits wide
  assign Xor = in_2 ^ in_4;  // XOR_Gate xor_1, 32 bits wide
  SLT slt_1 (.B(in_2), .A(in_4), .NoSign(in_6), .Output(Slt));
  Mult mult_1 (.in_1(in_2), .in_2(in_4), .in_3(in_6), .Output_2(MultHi), .Output(MultLo));
  Div div_1 (.in_1(in_2), .in_2(in_4), .in_3(in_6), .LO(DivLo), .HI(DivHi));
  Multiplexer #(.select(4), .width(32), .enable("false")) multiplexer_1 (
    .in1(Add), .in2(Sub), .in3(And), .in4(Or), .in5(Xor), .in6(Nor), .in7(Slt), .out(Output_2), .sel(in_5));  // open: in0, in8, in9, in10, in11, in12, in13, in14, in15
  Comparator #(.width(4)) comparator_1 (.a(in_5), .b(4'b0000), .eq(Mult));  // open: gt, lt
  Comparator #(.width(4)) comparator_2 (.a(in_5), .b(4'b1111), .eq(Div));  // open: gt, lt
  Multiplexer #(.width(32), .enable("false")) multiplexer_2 (
    .in0(MultLo), .in1(DivLo), .out(multiplexer_2_out), .sel(Div));
  Multiplexer #(.width(32), .enable("false")) multiplexer_3 (
    .in0(MultHi), .in1(DivHi), .out(multiplexer_3_out), .sel(Div));
  or or_2 (or_2_out, Mult, Div);
  Register #(.width(32)) register_1 (.D(multiplexer_2_out), .en(Enable), .Q(Output), .clk(in_1));  // open: clr
  Register #(.width(32)) register_2 (.D(multiplexer_3_out), .en(Enable), .Q(Output_3), .clk(in_1));  // open: clr
  and and_2 (Enable, or_2_out, in_3);

  // Other names for the same wires on the sheet: A[31:0] = in_2; B[31:0] = in_4; Clk = in_1; Hi[31:0] = Output_3;
  //   Lo[31:0] = Output; NoSign = in_6; On = in_3; OpSelect[3:0] = in_5
endmodule

module Operation_Select (
  input  in_1,
  input  in_2,
  input  in_3,
  input  in_4,
  input  in_5,
  input  in_6,
  input  in_7,
  input  in_8,
  input  in_9,
  input  in_10,
  input  in_11,
  input  in_12,
  input  in_13,
  input  in_14,
  input  in_15,
  input  in_16,
  input  in_17,
  input  in_18,
  output [3:0] Selector,
  output NoSign,
  output Inmediate,
  output ALU_ON
);

  wire Add_Addi, All_Slt, And_Andi, Mult_Mulu, Or_Ori, Xor_Xori;

  or or_1 (Add_Addi, in_1, in_2);
  or or_2 (And_Andi, in_5, in_6);
  or or_3 (Or_Ori, in_9, in_10);
  or or_4 (Xor_Xori, in_13, in_14);
  or or_5 (Mult_Mulu, in_3, in_4);
  or or_6 (Selector[3], in_7, in_8);
  or or_7 (All_Slt, in_11, in_15, in_12, in_16);
  or or_8 (NoSign, in_4, in_8, in_15, in_16);
  or or_9 (Selector[0], Add_Addi, And_Andi, Xor_Xori, All_Slt, Selector[3]);
  or or_10 (Inmediate, in_2, in_6, in_10, in_14, in_12);
  or or_11 (Selector[1], in_18, And_Andi, in_17, All_Slt, Selector[3]);
  or or_12 (ALU_ON, Selector[0], Selector[1], Selector[2], Selector[3], Mult_Mulu);
  or or_13 (Selector[2], Or_Ori, Xor_Xori, in_17, All_Slt, Selector[3]);

  // Other names for the same wires on the sheet: Add = in_1; Addi = in_2; And = in_5; Andi = in_6; Div = in_7;
  //   Divu = in_8; Mult = in_3; Mulu = in_4; Nor = in_17; Or = in_9; Ori = in_10; _1 = Selector[0]; _2 = Selector[1];
  //   _3 = Selector[2]; Div_Divu = Selector[3]; Slt = in_11; Slti = in_12; Sltiu = in_16; Sltu = in_15; Sub = in_18;
  //   Xor = in_13; Xori = in_14
endmodule

// MA
module Memory_Address (
  input  [31:0] ALU_Result,
  input  [31:0] PC,
  input  [31:0] SP,
  input  Pop,
  input  Push,
  input  Lw,
  input  Sw,
  input  PCout,
  output [31:0] Output
);

  wire [1:0] SelectOut;
  wire [31:0] multiplexer_1_out, subtractor_1_out;

  or or_1 (SelectOut[0], Push, Pop, PCout);
  or or_2 (SelectOut[1], Lw, Sw, PCout);
  Subtractor #(.width(32)) subtractor_1 (.a(SP), .b(32'h4), .out(subtractor_1_out));  // open: bin, bout
  Multiplexer #(.width(32), .enable("false")) multiplexer_1 (
    .in0(SP), .in1(subtractor_1_out), .out(multiplexer_1_out), .sel(Push));
  Multiplexer #(.select(2), .width(32), .enable("false")) multiplexer_2 (
    .in0(PC), .in1(multiplexer_1_out), .in2(ALU_Result), .in3(PC), .out(Output), .sel(SelectOut));
endmodule

module DataPath (
  input  clk,
  input  [6:0] KeyboardInput,
  input  [31:0] Instruction,
  input  Reset,
  input  KeyboardAva,
  input  EnablerRF,
  input  EnablerPC,
  input  EnablerGI,
  input  NextOk,
  output WriteI,
  output ALUI,
  output StackI,
  output MemoryI,
  output Tty,
  output JumpI,
  output RI,
  output Halt,
  output [6:0] TtyData,
  output [31:0] Address,
  output [31:0] ROut
);

  wire Add, Addi, AddiO, AluOn, And, Andi, Beq, Bgtz, Blez, Bltz, Bne, Div, Divu, Inmediate, J, Jr, Kbd, Lw,
       Mfhi, Mflo, Mult, Mulu, No_Andi_Xori_Ori, Nop, Nor, NoSign, Or, Ori, Pop, Push, Rnd, Slt, Slti, Sltiu,
       Sltu, Sub, Sw, Xor, Xori;
  wire [2:0] SelectRF;
  wire [3:0] SelectALU;
  wire [4:0] Dest, Rd, Rs_t, Rt_t;
  wire [15:0] Constante;
  wire [25:0] DestinoSalto;
  wire [31:0] ALUR, branch_control_1_output, Hi, instruction_1_output, KeyboardInput32, Lo, PC, Random,
       RFInput, Rt, Rt_Const, SP;
  wire [31:7] Rs;
  wire [31:31] and_2_out;

  or or_1 (AddiO, Sw, Lw, Addi);
  and and_1 (No_Andi_Xori_Ori, ~Xori, ~Andi, ~Ori);  // AND_Gate
  Instruction instruction_1 (
    .Inst(Instruction), .Clk(clk), .Reset(Reset), .Enable(EnablerGI), .Output(instruction_1_output));
  Multiplexer #(.width(5)) multiplexer_1 (.in0(Rd), .in1(Rt_t), .out(Dest), .sel(Inmediate));  // open: en
  assign KeyboardInput32 = {{25{1'b0}}, KeyboardInput};  // Bit_Extender bit_extender_1
  Random #(.width(32)) random_1 (.clk(clk), .next(Rnd), .out(Random));  // open: clr
  // Probe on instruction_1_output
  // Probe on Rs_t
  Register_File register_file_1 (
    .clk(clk), .reset(Reset), .write(EnablerRF), .pop(Pop), .Dest(Dest), .push(Push), .A(Rs_t),
    .PCEn(EnablerPC), .B(Rt_t), .StackPointer(SP), .Output_A({Rs, TtyData}), .Output_B(Rt), .Input(RFInput));
  and and_2 (and_2_out[31], No_Andi_Xori_Ori, Constante[15]);
  Instruction_Decoder u_Sw (
    .Nop(Nop), .Slt(Slt), .Jr(Jr), .Addi(Addi), .Sw(Sw), .Addt(Add), .Sltu(Sltu), .Mfhi(Mfhi), .Slti(Slti),
    .Beq(Beq), .in_1(instruction_1_output), .Sub(Sub), .And(And), .Mflo(Mflo), .Sltiu(Sltiu), .Bne(Bne),
    .Mult(Mult), .Or(Or), .Halt(Halt), .Andi(Andi), .Blez(Blez), .Div(Div), .Nor(Nor), .Tty(Tty), .Ori(Ori),
    .Bgtz(Bgtz), .Mulu(Mulu), .Xor(Xor), .Rnd(Rnd), .Xori(Xori), .Bltz(Bltz), .Divu(Divu), .Pop(Pop),
    .Kbd(Kbd), .Lw(Lw), .J(J), .Push(Push), .DestinoSalto(DestinoSalto), .Constante(Constante), .RS(Rs_t),
    .RT(Rt_t), .RD(Rd));
  Multiplexer #(.width(32), .enable("false")) multiplexer_2 (
    .in0(Rt), .in1({{16{and_2_out[31]}}, Constante}), .out(Rt_Const), .sel(Inmediate));
  Operation_Select operation_select_1 (
    .in_1(Add), .in_2(AddiO), .in_3(Mult), .in_4(Mulu), .in_5(And), .in_6(Andi), .in_7(Div), .in_8(Divu),
    .in_9(Or), .in_10(Ori), .in_11(Slt), .in_12(Slti), .in_13(Xor), .in_14(Xori), .in_15(Sltu),
    .in_16(Sltiu), .in_17(Nor), .in_18(Sub), .Selector(SelectALU), .NoSign(NoSign), .Inmediate(Inmediate),
    .ALU_ON(AluOn));
  or or_2 (SelectRF[0], Lw, Pop, Mflo, Kbd);
  or or_3 (SelectRF[1], Mflo, Mfhi);
  or or_4 (SelectRF[2], Kbd, Rnd);
  // Probe on SP
  ALU alu_1 (
    .in_2({Rs, TtyData}), .in_4(Rt_Const), .in_5(SelectALU), .in_6(NoSign), .Output_2(ALUR), .in_1(clk),
    .in_3(AluOn), .Output(Lo), .Output_3(Hi));
  // Probe on SelectALU
  Memory_Address memory_address_1 (
    .ALU_Result(ALUR), .PC(PC), .SP(SP), .Pop(Pop), .Push(Push), .Lw(Lw), .Sw(Sw), .PCout(NextOk),
    .Output(Address));
  // Probe on Lo
  or or_5 (ALUI, Mulu, Add, Or, Addi, Div, And, Ori, Andi, Xor, Divu, Mult, Xori, Sub, Nor, Sltiu, Sltu, Slti, Slt);
  or or_6 (JumpI, Bne, Nop, Beq, Bgtz, J, Bltz, Jr, Blez);
  // Probe on RFInput
  Multiplexer #(.select(3), .width(32), .enable("false")) multiplexer_3 (
    .in0(ALUR), .in1(Instruction), .in2(Hi), .in3(Lo), .in4(Random), .in5(KeyboardInput32), .out(RFInput),
    .sel(SelectRF));  // open: in6, in7
  or or_7 (WriteI, Push, Sw);
  or or_8 (StackI, Pop, Push);
  or or_9 (MemoryI, Sw, Lw);
  or or_10 (RI, Mflo, Tty, Mfhi, Rnd, Kbd);
  Multiplexer #(.width(32), .enable("false")) multiplexer_4 (.in0({Rs, TtyData}), .in1(Rt), .out(ROut), .sel(Sw));
  Branch_Control branch_control_1 (
    .in_1({Rs, TtyData}), .in_2(PC), .in_3(DestinoSalto), .in_4(Constante), .in_5(Beq), .in_6(Bgtz),
    .in_7(J), .in_8(Rt), .in_9(Bne), .in_10(Bltz), .in_11(Jr), .in_12(Blez), .Output(branch_control_1_output));
  Program_Counter program_counter_1 (
    .in_2(EnablerPC), .in_3(Reset), .in_1(branch_control_1_output), .Output(PC), .in_4(clk));

  // Other names for the same wires on the sheet: Rs[6:0] = TtyData
endmodule

// CU
module Control_Unit (
  input  Clk,
  input  Start,
  input  ReadyData,
  input  AluI,
  input  JumpI,
  input  MemoryI,
  input  RI,
  input  Reset,
  input  ReadyI,
  input  WriteI,
  input  ReadyW,
  input  TtyI,
  output End,
  output TtyEn,
  output Write,
  output GetData,
  output UseGI,
  output UseRF,
  output KeyboardEN,
  output GetI,
  output UsePC
);

  wire Branch, d_ff_1_q, d_ff_2_q, d_ff_3_q, d_ff_5_q, demultiplexer_1_out0, demultiplexer_1_out1, or_5_out,
       RF;
  wire [2:0] SelectOut;

  D_Flip_Flop #(.trigger("falling")) d_ff_1 (
    .clk(Clk), .D(Start), .Q(d_ff_1_q), .reset(Reset));  // open: Qn, preset, en
  D_Flip_Flop #(.trigger("falling")) d_ff_2 (
    .clk(Clk), .D(ReadyI), .Q(d_ff_2_q), .reset(Reset));  // open: Qn, preset, en
  D_Flip_Flop #(.trigger("falling")) d_ff_3 (
    .clk(Clk), .D(UsePC), .Q(d_ff_3_q), .reset(Reset));  // open: Qn, preset, en
  or or_1 (SelectOut[0], RI, AluI, WriteI);
  or or_2 (SelectOut[1], RI, JumpI);
  or or_3 (SelectOut[2], MemoryI, WriteI);
  or or_4 (GetI, d_ff_1_q, d_ff_3_q);
  Demultiplexer #(.select(3), .enable("false")) demultiplexer_1 (
    .out0(demultiplexer_1_out0), .out1(demultiplexer_1_out1), .out2(Branch), .out3(RF), .out4(GetData),
    .out5(Write), .in(d_ff_2_q), .sel(SelectOut));  // open: out6, out7
  or or_5 (or_5_out, End, demultiplexer_1_out0);
  D_Flip_Flop #(.trigger("falling")) d_ff_4 (.clk(Clk), .D(or_5_out), .Q(End), .reset(Reset));  // open: Qn, preset, en
  D_Flip_Flop #(.trigger("falling")) d_ff_5 (
    .clk(Clk), .D(demultiplexer_1_out1), .Q(d_ff_5_q), .reset(Reset));  // open: Qn, preset, en
  and and_1 (TtyEn, KeyboardEN, TtyI);
  or or_6 (UseRF, d_ff_5_q, ReadyData, RF);
  D_Flip_Flop #(.trigger("falling")) d_ff_6 (.clk(Clk), .D(UseRF), .Q(KeyboardEN));  // open: Qn, preset, en, reset
  or or_7 (UsePC, KeyboardEN, ReadyW, Branch);

  assign UseGI = ReadyI;

  // Other names for the same wires on the sheet: Cont = UsePC; Tty = KeyboardEN
endmodule

// RM
module Read_Ram (
  input  [31:0] Bank0,
  input  [31:0] Bank1,
  input  [31:0] Bank2,
  input  [31:0] Bank3,
  input  [15:0] ADDR,
  input  [3:0] ReadTime,
  input  Clk,
  input  Reset,
  input  Get,
  input  Write,
  output [31:0] BankOut0,
  output [31:0] BankOut1,
  output [31:0] BankOut2,
  output [31:0] BankOut3,
  output Ready,
  output CS
);

  wire a, and_3_out, and_4_out, comparator_1_eq, Cont, d_ff_4_q, GetRead, multiplexer_1_out, not_1_out,
       or_1_out, ReadyRead, ResetMem, RM, Stop, X;
  wire [15:0] ADDRMem;

  Register #(.width(16)) register_1 (.D(ADDR), .en(X), .Q(ADDRMem), .clk(Clk), .clr(Reset));
  D_Flip_Flop #(.trigger("falling")) d_ff_1 (.clk(Clk), .D(GetRead), .Q(a), .en(or_1_out));  // open: Qn, preset, reset
  or or_1 (or_1_out, GetRead, Stop);
  not not_1 (not_1_out, Cont);
  and and_1 (GetRead, Get, not_1_out);
  Comparator #(.width(16)) comparator_1 (.a(ADDR), .b(ADDRMem), .eq(comparator_1_eq));  // open: gt, lt
  Timer timer_1 (.in_1(a), .in_2(ReadyRead), .in_3(Clk), .in_4(ReadTime), .Ready(Stop));
  and and_2 (Cont, ~ResetMem, comparator_1_eq);  // AND_Gate
  D_Flip_Flop #(.trigger("falling")) d_ff_2 (.clk(Clk), .D(Stop), .Q(X), .reset(ReadyRead));  // open: Qn, preset, en
  D_Flip_Flop #(.trigger("falling")) d_ff_3 (.clk(Clk), .D(X), .Q(ReadyRead));  // open: Qn, preset, en, reset
  or or_2 (CS, X, a);
  and and_3 (and_3_out, Cont, Write);
  or or_3 (RM, and_3_out, Reset);
  Register #(.width(32)) register_2 (.D(Bank0), .en(X), .Q(BankOut0), .clk(Clk), .clr(Reset));
  Register #(.width(32)) register_3 (.D(Bank2), .en(X), .Q(BankOut2), .clk(Clk), .clr(Reset));
  and and_4 (and_4_out, Get, Cont);
  Multiplexer #(.enable("false")) multiplexer_1 (.in0(ResetMem), .in1(RM), .out(multiplexer_1_out), .sel(RM));
  D_Flip_Flop #(.trigger("falling")) d_ff_4 (
    .clk(Clk), .D(and_4_out), .Q(d_ff_4_q), .reset(Reset));  // open: Qn, preset, en
  D_Flip_Flop #(.trigger("falling")) d_ff_5 (
    .clk(Clk), .D(multiplexer_1_out), .Q(ResetMem), .reset(ReadyRead));  // open: Qn, preset, en
  Register #(.width(32)) register_4 (.D(Bank1), .en(X), .Q(BankOut1), .clk(Clk), .clr(Reset));
  Register #(.width(32)) register_5 (.D(Bank3), .en(X), .Q(BankOut3), .clk(Clk), .clr(Reset));
  or or_4 (Ready, ReadyRead, d_ff_4_q);
endmodule

// RI
module Ram_Interact (
  input  [31:0] Bank0,
  input  [31:0] Bank1,
  input  [31:0] Bank2,
  input  [31:0] Bank3,
  input  [31:0] DPAddress,
  input  [3:0] ReadTime,
  input  [3:0] WriteTime,
  input  Clk,
  input  Reset,
  input  Write,
  input  GetI,
  input  GetData,
  input  IsI,
  output [31:0] BankOut0,
  output [31:0] BankOut1,
  output [31:0] BankOut2,
  output [31:0] BankOut3,
  output [3:0] MASK,
  output [15:0] ADDR,
  output RW,
  output CS,
  output ReadyI,
  output ReadyData,
  output ReadyWrite
);

  wire CSD, CSI, or_1_out, Stop0;
  wire [31:0] DO0, DO1, DO2, DO3, i_o_1_output, i_o_2_output, i_o_3_output, i_o_4_output, IO0, IO1, IO2, IO3;

  D_Flip_Flop #(.trigger("falling")) d_ff_1 (.clk(Clk), .D(Write), .Q(RW), .en(or_1_out));  // open: Qn, preset, reset
  or or_1 (or_1_out, Write, Stop0);
  Read_Ram read_ram_1 (
    .Bank0(Bank0), .Bank1(Bank1), .Bank2(Bank2), .Bank3(Bank3), .ADDR(DPAddress[19:4]), .ReadTime(ReadTime),
    .Clk(Clk), .Reset(Reset), .Get(GetI), .Write(Write), .BankOut0(IO0), .BankOut1(IO1), .BankOut2(IO2),
    .BankOut3(IO3), .Ready(ReadyI), .CS(CSI));
  Timer timer_1 (.in_1(RW), .in_2(ReadyWrite), .in_3(Clk), .in_4(WriteTime), .Ready(Stop0));
  D_Flip_Flop #(.trigger("falling")) d_ff_2 (.clk(Clk), .D(Stop0), .Q(ReadyWrite));  // open: Qn, preset, en, reset
  Read_Ram read_ram_2 (
    .Bank0(Bank0), .Bank1(Bank1), .Bank2(Bank2), .Bank3(Bank3), .ADDR(DPAddress[19:4]), .ReadTime(ReadTime),
    .Clk(Clk), .Reset(Reset), .Get(GetData), .Write(Write), .BankOut0(DO0), .BankOut1(DO1), .BankOut2(DO2),
    .BankOut3(DO3), .Ready(ReadyData), .CS(CSD));
  or or_2 (CS, RW, CSI, CSD);
  I_O i_o_1 (.in_1(DO0), .Output(i_o_1_output));
  I_O i_o_2 (.in_1(DO1), .Output(i_o_2_output));
  I_O i_o_3 (.in_1(DO2), .Output(i_o_3_output));
  I_O i_o_4 (.in_1(DO3), .Output(i_o_4_output));
  Multiplexer #(.width(32), .enable("false")) multiplexer_1 (.in0(i_o_1_output), .in1(IO0), .out(BankOut0), .sel(IsI));
  Multiplexer #(.width(32), .enable("false")) multiplexer_2 (.in0(i_o_2_output), .in1(IO1), .out(BankOut1), .sel(IsI));
  Multiplexer #(.width(32), .enable("false")) multiplexer_3 (.in0(i_o_3_output), .in1(IO2), .out(BankOut2), .sel(IsI));
  Multiplexer #(.width(32), .enable("false")) multiplexer_4 (.in0(i_o_4_output), .in1(IO3), .out(BankOut3), .sel(IsI));
  Demultiplexer #(.select(2), .enable("false")) demultiplexer_1 (
    .out0(MASK[0]), .out1(MASK[1]), .out2(MASK[2]), .out3(MASK[3]), .in(1'b1), .sel(DPAddress[3:2]));

  assign ADDR = DPAddress[19:4];
endmodule

module SLT (
  input  [31:0] B,
  input  [31:0] A,
  input  NoSign,
  output [31:0] Output
);

  wire and_1_out, and_2_out, comparator_1_lt, comparator_2_lt;

  Comparator #(.width(32)) comparator_1 (.a(B), .b(A), .lt(comparator_1_lt));  // open: gt, eq
  Comparator #(.width(32), .mode("unsigned")) comparator_2 (.a(B), .b(A), .lt(comparator_2_lt));  // open: gt, eq
  and and_1 (and_1_out, comparator_1_lt, ~NoSign);  // AND_Gate
  and and_2 (and_2_out, NoSign, comparator_2_lt);
  or or_1 (Output[0], and_1_out, and_2_out);

  assign Output[31:1] = {31{1'b0}};

  // Other names for the same wires on the sheet: A_t[31:0] = B; B_t[31:0] = A; IsLess = Output[0]
endmodule

module Mult (
  input  [31:0] in_1,
  input  [31:0] in_2,
  input  in_3,
  output [31:0] Output,
  output [31:0] Output_2
);

  wire adder_1_cout, Sel, SignA, SignB, xor_1_out;
  wire [31:0] AbsA, AbsB, bit_extender_1_out, HI, HIC2, LO, LOC2, not_1_out, not_2_out;

  Abs abs_1 (.in_1(in_1), .in_2(in_3), .Output_2(SignA), .Output(AbsA));
  Abs abs_2 (.in_1(in_2), .in_2(in_3), .Output_2(SignB), .Output(AbsB));
  Multiplier #(.width(32)) multiplier_1 (.a(AbsA), .b(AbsB), .out(LO), .cout(HI));  // open: cin
  xor xor_1 (xor_1_out, SignA, SignB);
  assign not_1_out = ~LO;  // NOT_Gate not_1, 32 bits wide
  Multiplexer #(.width(32), .enable("false")) multiplexer_1 (.in0(LO), .in1(LOC2), .out(Output), .sel(Sel));
  and and_1 (Sel, ~in_3, xor_1_out);  // AND_Gate
  Adder #(.width(32)) adder_1 (.a(not_1_out), .b(32'h1), .out(LOC2), .cout(adder_1_cout));  // open: cin
  assign not_2_out = ~HI;  // NOT_Gate not_2, 32 bits wide
  assign bit_extender_1_out = {{31{1'b0}}, adder_1_cout};  // Bit_Extender bit_extender_1
  Multiplexer #(.width(32), .enable("false")) multiplexer_2 (.in0(HI), .in1(HIC2), .out(Output_2), .sel(Sel));
  Adder #(.width(32)) adder_2 (.a(not_2_out), .b(bit_extender_1_out), .out(HIC2));  // open: cin, cout

  // Other names for the same wires on the sheet: A[31:0] = in_1; B[31:0] = in_2; NoSign = in_3;
  //   OutHI[31:0] = Output_2; OutLO[31:0] = Output
endmodule

module Div (
  input  [31:0] in_1,
  input  [31:0] in_2,
  input  in_3,
  output [31:0] LO,
  output [31:0] HI
);

  wire [31:0] HIS, HIU, LOS, LOU, multiplexer_1_out, multiplexer_2_out, negator_1_out, negator_2_out;

  Negator #(.width(32)) negator_1 (.in(in_1), .out(negator_1_out));
  Negator #(.width(32)) negator_2 (.in(in_2), .out(negator_2_out));
  Divider #(.width(32)) divider_1 (.a(in_1), .b(in_2), .out(LOU), .rem(HIU));  // open: upper
  Multiplexer #(.width(32), .enable("false")) multiplexer_1 (
    .in0(in_1), .in1(negator_1_out), .out(multiplexer_1_out), .sel(in_1[31]));
  Multiplexer #(.width(32), .enable("false")) multiplexer_2 (
    .in0(in_2), .in1(negator_2_out), .out(multiplexer_2_out), .sel(in_2[31]));
  Divider #(.width(32)) divider_2 (.a(multiplexer_1_out), .b(multiplexer_2_out), .out(LOS), .rem(HIS));  // open: upper
  Multiplexer #(.width(32), .enable("false")) multiplexer_3 (.in0(LOS), .in1(LOU), .out(LO), .sel(in_3));
  Multiplexer #(.width(32), .enable("false")) multiplexer_4 (.in0(HIS), .in1(HIU), .out(HI), .sel(in_3));

  // Other names for the same wires on the sheet: A[31:0] = in_1; SignA = in_1[31]; B[31:0] = in_2; SignB = in_2[31];
  //   NoSign = in_3
endmodule

module Abs (
  input  [31:0] in_1,
  input  in_2,
  output [31:0] Output,
  output Output_2
);

  wire and_1_out;
  wire [31:0] negator_1_out;

  Negator #(.width(32)) negator_1 (.in(in_1), .out(negator_1_out));
  Multiplexer #(.width(32), .enable("false")) multiplexer_1 (
    .in0(in_1), .in1(negator_1_out), .out(Output), .sel(and_1_out));
  and and_1 (and_1_out, in_1[31], ~in_2);  // AND_Gate

  assign Output_2 = in_1[31];

  // Other names for the same wires on the sheet: bit31 = in_1[31]; NoSign = in_2
endmodule

// Inst
module Instruction (
  input  [31:0] Inst,
  input  Clk,
  input  Reset,
  input  Enable,
  output [31:0] Output
);

  Register #(.width(32)) register_1 (
    .D(Inst), .en(Enable), .Q({Output[7:0], Output[15:8], Output[23:16], Output[31:24]}), .clk(Clk),
    .clr(Reset));
endmodule

module Timer (
  input  in_1,
  input  in_2,
  input  in_3,
  input  [3:0] in_4,
  output Ready
);

  wire [3:0] counter_1_q;

  Counter #(.width(4), .max('hf)) counter_1 (
    .count(in_1), .Q(counter_1_q), .clk(in_3), .clr(in_2));  // open: load, D, carry
  Comparator #(.width(4)) comparator_1 (.a(in_4), .b(counter_1_q), .eq(Ready));  // open: gt, lt

  // Other names for the same wires on the sheet: Clk = in_3; Reset = in_2; Start = in_1; Time[3:0] = in_4
endmodule

module I_O (
  input  [31:0] in_1,
  output [31:0] Output
);


  assign Output = {in_1[7:0], in_1[15:8], in_1[23:16], in_1[31:24]};
endmodule
